// Logisim project MicroCPU.circ as structural Verilog: 8 circuits, main circuit CPU
module UC (
  input  [1:0] JMP,
  input  [1:0] RgIN,
  input  [1:0] RgTO,
  input  [3:0] Reg1,
  input  [3:0] ULA_TO,
  input  [3:0] Reg2,
  output ClearREG,
  output ClearCNT,
  output LOAD1,
  output LOAD2,
  output [3:0] Reg1_TO,
  output [3:0] ULA_IN,
  output [3:0] Reg2_TO
);

  wire and_2_out, and_6_out;

  and and_1 (ClearREG, ~JMP[1], JMP[0]);  // AND_Gate
  Multiplexer #(.width(4), .enable("false")) multiplexer_1 (.in0(Reg1), .in1(Reg2), .out(ULA_IN), .sel(and_2_out));
  and and_2 (and_2_out, RgIN[1], ~RgIN[0]);  // AND_Gate
  and and_3 (ClearCNT, JMP[1], ~JMP[0]);  // AND_Gate
  and and_4 (LOAD1, ~RgTO[1], RgTO[0]);  // AND_Gate
  and and_5 (LOAD2, RgTO[1], ~RgTO[0]);  // AND_Gate
  Demultiplexer #(.width(4), .enable("false")) demultiplexer_1 (
    .out0(Reg1_TO), .out1(Reg2_TO), .in(ULA_TO), .sel(and_6_out));
  and and_6 (and_6_out, RgTO[1], ~RgTO[0]);  // AND_Gate
endmodule

module CPU (
);

  wire ClearCNT, ClearREG, K0, K1, K2, K3, L0, L1, L2, L3, L4, L5, L6, L7, L8, L9, LOAD1, LOAD2, not_1_out,
       not_2_out, not_3_out, not_4_out, or_1_out, or_2_out, or_3_out, S0, S1, S2, S3, S4, S5, S6, S7, S8, S9;
  wire [1:1] and_1_out;
  wire [3:0] HEX0, HEX1, HEX2, HEX3, HEX4, HEX5, Reg1_TO, Reg2_TO, ULA_IN, ULA_TO;

  Hex_Digit_Display hex_digit_display_1 (.value(HEX5));  // open: dp
  LED u_L8 (.in(L8));
  LED u_L9 (.in(L9));
  // DipSwitch #(.NSwitches(1)) S9: pin names not known; wires that end beside it: S9
  // DipSwitch #(.NSwitches(1)) S8: pin names not known; wires that end beside it: S8
  Hex_Digit_Display hex_digit_display_2 (.value(HEX3));  // open: dp
  Hex_Digit_Display hex_digit_display_3 (.value(HEX4));  // open: dp
  LED u_L6 (.in(L6));
  LED u_L5 (.in(L5));
  LED u_L7 (.in(L7));
  // DipSwitch #(.NSwitches(1)) S7: pin names not known; wires that end beside it: S7
  // DipSwitch #(.NSwitches(1)) S5: pin names not known; wires that end beside it: S5
  // DipSwitch #(.NSwitches(1)) S6: pin names not known; wires that end beside it: S6
  Hex_Digit_Display hex_digit_display_4 (.value(HEX2));  // open: dp
  LED u_L3 (.in(L3));
  LED u_L4 (.in(L4));
  // DipSwitch #(.NSwitches(1)) S2: pin names not known; wires that end beside it: S2
  // DipSwitch #(.NSwitches(1)) S4: pin names not known; wires that end beside it: S4
  // DipSwitch #(.NSwitches(1)) S3: pin names not known; wires that end beside it: S3
  not not_1 (not_1_out, S9);
  and and_1 (and_1_out[1], not_1_out, HEX4[2], HEX4[3]);
  UC uc_1 (
    .JMP(HEX4[3:2]), .Reg1(HEX1), .ULA_TO(ULA_TO), .Reg2(HEX0), .RgTO(HEX5[3:2]), .RgIN(HEX5[1:0]),
    .ClearCNT(ClearCNT), .ClearREG(ClearREG), .Reg1_TO(Reg1_TO), .ULA_IN(ULA_IN), .Reg2_TO(Reg2_TO),
    .LOAD2(LOAD2), .LOAD1(LOAD1));
  Hex_Digit_Display hex_digit_display_5 (.value(HEX1));  // open: dp
  Hex_Digit_Display hex_digit_display_6 (.value(HEX0));  // open: dp
  LED u_L1 (.in(L1));
  LED u_L0 (.in(L0));
  LED u_L2 (.in(L2));
  // DipSwitch #(.NSwitches(1)) S0: pin names not known; wires that end beside it: S0
  // DipSwitch #(.NSwitches(1)) S1: pin names not known; wires that end beside it: S1
  not not_2 (not_2_out, S9);
  Button u_K3 (.out(K3));
  Button u_K2 (.out(K2));
  Count8 Count8 (
    .CLK(not_2_out), .OUT({L7, L6, L5, L4, L3, L2, L1, L0}), .OPER(HEX2), .JMP({2{and_1_out[1]}}),
    .CLR(or_1_out));
  or or_1 (or_1_out, S0, ClearCNT);
  Button u_K1 (.out(K1));
  Button u_K0 (.out(K0));
  ROM_256x16 ROM_256x16 (
    .ROM_ADRESS({L7, L6, L5, L4, L3, L2, L1, L0}), .CLK(S9), .ROM_OUT({HEX5, HEX4, HEX3, HEX2}), .CLR(S0));
  Reg4 Reg4_1 (.CLK(not_3_out), .Load(LOAD1), .Clear(or_2_out), .In(Reg1_TO), .Out(HEX1));
  not not_3 (not_3_out, S9);
  or or_2 (or_2_out, ClearREG, S0);
  ULA4 ULA (.RgIn(ULA_IN), .Oper(HEX2), .ULA(HEX4[1:0]), .RgTo(ULA_TO));
  Reg4 Reg4_2 (.CLK(not_4_out), .Load(LOAD2), .Clear(or_3_out), .In(Reg2_TO), .Out(HEX0));
  not not_4 (not_4_out, S9);
  or or_3 (or_3_out, ClearREG, S0);

  // Other names for the same wires on the sheet: OPER[3:0] = HEX2; JMP[1:0] = HEX4[3:2]; Reg1[3:0] = HEX1;
  //   Reg2[3:0] = HEX0; RgIN[1:0] = HEX5[1:0]; RgTO[1:0] = HEX5[3:2]; ULA[1:0] = HEX4[1:0]
endmodule

module ROM_256x16 (
  input  [7:0] ROM_ADRESS,
  input  CLK,
  input  CLR,
  output [15:0] ROM_OUT
);

  wire [15:0] ROM_256x16_data;

  ROM #(.dataWidth(16), .Select("low")) ROM_256x16 (.addr(ROM_ADRESS), .data(ROM_256x16_data));
  Register #(.width(16), .Select("low")) register_1 (
    .D(ROM_256x16_data), .Q(ROM_OUT), .clk(CLK), .clr(CLR));  // open: en

  // Notes on the sheet:
  //   contents of ROM_256x16 (hex, n*v repeats v):
  //   6005 9101 6202 6304 c08 0 0 0 400 6001 9001 9002 6302 6102 9302 6200 6001 800
endmodule

module Reg4 (
  input  [3:0] In,
  input  CLK,
  input  Load,
  input  Clear,
  output [3:0] Out
);

  wire multiplexer_1_out, multiplexer_2_out, multiplexer_3_out, multiplexer_4_out;

  Multiplexer #(.enable("false")) multiplexer_1 (.in0(Out[0]), .in1(In[0]), .out(multiplexer_1_out), .sel(Load));
  D_Flip_Flop d_ff_1 (.clk(CLK), .D(multiplexer_1_out), .Q(Out[0]), .reset(Clear));  // open: Qn, preset
  Multiplexer #(.enable("false")) multiplexer_2 (.in0(Out[1]), .in1(In[1]), .out(multiplexer_2_out), .sel(Load));
  D_Flip_Flop d_ff_2 (.clk(CLK), .D(multiplexer_2_out), .Q(Out[1]), .reset(Clear));  // open: Qn, preset
  Multiplexer #(.enable("false")) multiplexer_3 (.in0(Out[2]), .in1(In[2]), .out(multiplexer_3_out), .sel(Load));
  D_Flip_Flop d_ff_3 (.clk(CLK), .D(multiplexer_3_out), .Q(Out[2]), .reset(Clear));  // open: Qn, preset
  Multiplexer #(.enable("false")) multiplexer_4 (.in0(Out[3]), .in1(In[3]), .out(multiplexer_4_out), .sel(Load));
  D_Flip_Flop d_ff_4 (.clk(CLK), .D(multiplexer_4_out), .Q(Out[3]), .reset(Clear));  // open: Qn, preset
endmodule

module ULA4 (
  input  [3:0] RgIn,
  input  [3:0] Oper,
  input  [1:0] ULA,
  output [3:0] RgTo
);

  wire [3:0] adder_1_out, divider_1_out, multiplier_1_out, subtractor_1_out;

  Adder #(.width(4)) adder_1 (.a(Oper), .b(RgIn), .out(adder_1_out));  // open: cin, cout
  Subtractor #(.width(4)) subtractor_1 (.a(RgIn), .b(Oper), .out(subtractor_1_out));  // open: bin, bout
  Divider #(.width(4)) divider_1 (.a(Oper), .b(4'b0010), .out(divider_1_out));  // open: upper, rem
  Multiplier #(.width(4)) multiplier_1 (.a(Oper), .b(4'b0010), .out(multiplier_1_out));  // open: cin, cout
  Multiplexer #(.select(2), .width(4), .enable("false")) multiplexer_1 (
    .in0(adder_1_out), .in1(multiplier_1_out), .in2(subtractor_1_out), .in3(divider_1_out), .out(RgTo),
    .sel(ULA));

  // Notes on the sheet:
  //   00
  //   10
  //   11
  //   01
endmodule

module Count8 (
  input  CLK,
  input  [3:0] OPER,
  input  [1:0] JMP,
  input  CLR,
  output [7:0] OUT
);

  wire and_1_out, or_1_out;

  or or_1 (or_1_out, JMP[1], CLR);
  Count4JMP count4jmp_1 (
    .Oper3(OPER[3]), .Oper2(OPER[2]), .Oper1(OPER[1]), .Oper0(OPER[0]), .JMP0(JMP[0]), .JMP1(or_1_out),
    .Clock(CLK), .Q0(OUT[0]), .Q1(OUT[1]), .Q2(OUT[2]), .out_11(OUT[3]));
  and and_1 (and_1_out, ~OUT[0], ~OUT[1], ~OUT[2], ~OUT[3]);  // AND_Gate
  Count4 count4_1 (.Clock(and_1_out), .Reset(or_1_out), .Q0(OUT[4]), .Q1(OUT[5]), .Q2(OUT[6]), .out_6(OUT[7]));

  // Other names for the same wires on the sheet: O0 = OUT[0]; O1 = OUT[1]; O2 = OUT[2]; O3 = OUT[3]; O4 = OUT[4];
  //   O5 = OUT[5]; O6 = OUT[6]; O7 = OUT[7]
endmodule

module Count4 (
  input  Clock,
  input  Reset,
  output Q0,
  output Q1,
  output Q2,
  output out_6
);

  wire and_1_out, and_2_out, not_1_out;

  not not_1 (not_1_out, 1'b0);
  J_K_Flip_Flop j_k_ff_1 (.J(not_1_out), .clk(Clock), .K(not_1_out), .Q(Q0), .reset(Reset));  // open: Qn, preset
  J_K_Flip_Flop j_k_ff_2 (.J(Q0), .clk(Clock), .K(Q0), .Q(Q1), .reset(Reset));  // open: Qn, preset
  and and_1 (and_1_out, Q1, Q0);
  J_K_Flip_Flop j_k_ff_3 (.J(and_1_out), .clk(Clock), .K(and_1_out), .Q(Q2), .reset(Reset));  // open: Qn, preset
  and and_2 (and_2_out, Q2, and_1_out);
  J_K_Flip_Flop j_k_ff_4 (.J(and_2_out), .clk(Clock), .K(and_2_out), .Q(out_6), .reset(Reset));  // open: Qn, preset
endmodule

module Count4JMP (
  input  Oper3,
  input  Oper2,
  input  Oper1,
  input  Oper0,
  input  JMP0,
  input  JMP1,
  input  Clock,
  output Q0,
  output Q1,
  output Q2,
  output out_11
);

  wire and_1_out, and_2_out, and_3_out, and_4_out, and_5_out, and_6_out, and_7_out, and_8_out, and_9_out,
       and_10_out, and_11_out, and_12_out, not_1_out, not_2_out, not_3_out, not_4_out, not_5_out, not_6_out,
       or_1_out, or_2_out, or_3_out, or_4_out;

  and and_1 (and_1_out, JMP1, JMP0);
  not not_1 (not_1_out, 1'b0);
  not not_2 (not_2_out, JMP0);
  and and_2 (and_2_out, JMP1, not_2_out);
  and and_3 (and_3_out, and_1_out, not_3_out);
  and and_4 (and_4_out, JMP1, JMP0, Oper0);
  J_K_Flip_Flop j_k_ff_1 (
    .J(not_1_out), .clk(Clock), .K(not_1_out), .Q(Q0), .preset(and_4_out), .reset(or_1_out));  // open: Qn
  or or_1 (or_1_out, and_3_out, and_2_out);
  not not_3 (not_3_out, Oper0);
  and and_5 (and_5_out, JMP1, JMP0, Oper1);
  or or_2 (or_2_out, and_6_out, and_2_out);
  and and_6 (and_6_out, and_1_out, not_4_out);
  not not_4 (not_4_out, Oper1);
  J_K_Flip_Flop j_k_ff_2 (.J(Q0), .clk(Clock), .K(Q0), .Q(Q1), .preset(and_5_out), .reset(or_2_out));  // open: Qn
  and and_7 (and_7_out, JMP1, JMP0, Oper2);
  J_K_Flip_Flop j_k_ff_3 (
    .J(and_8_out), .clk(Clock), .K(and_8_out), .Q(Q2), .preset(and_7_out), .reset(or_3_out));  // open: Qn
  or or_3 (or_3_out, and_9_out, and_2_out);
  and and_8 (and_8_out, Q1, Q0);
  and and_9 (and_9_out, and_1_out, not_5_out);
  not not_5 (not_5_out, Oper2);
  and and_10 (and_10_out, Q2, and_8_out);
  and and_11 (and_11_out, and_1_out, not_6_out);
  not not_6 (not_6_out, Oper3);
  and and_12 (and_12_out, JMP1, JMP0, Oper3);
  J_K_Flip_Flop j_k_ff_4 (
    .J(and_10_out), .clk(Clock), .K(and_10_out), .Q(out_11), .preset(and_12_out), .reset(or_4_out));  // open: Qn
  or or_4 (or_4_out, and_11_out, and_2_out);
endmodule
